// Logisim project CSE332_Rahiq_Tazrian.circ as structural Verilog: 5 circuits, main circuit main
module main (
  input  [7:0] in_1,
  input  Cin,
  input  in_3,
  input  in_4,
  input  in_5,
  input  CLK,
  output Cout
);

  wire [1:0] bit_extender_4_out;
  wire [4:0] bit_extender_1_out, bit_extender_2_out;
  wire [7:0] adder_1_out, PC_q;
  wire [31:0] bit_extender_3_out, n32_bit_alu_1_result, n32_bit_rf_1_data_out_1, ram_1_data, rom_1_data;

  Register PC (.D(adder_1_out), .Q(PC_q), .clk(CLK));  // open: en, clr
  Adder adder_1 (.a(PC_q), .b(8'h1), .out(adder_1_out));  // open: cin, cout
  ROM #(.dataWidth(32)) rom_1 (.addr(PC_q), .data(rom_1_data));  // open: sel
  Bit_Extender #(.out_width(5)) bit_extender_1 (.in(rom_1_data[23:16]), .out(bit_extender_1_out));
  Bit_Extender #(.out_width(5)) bit_extender_2 (.in(rom_1_data[15:8]), .out(bit_extender_2_out));
  assign bit_extender_3_out = {{24{1'b0}}, rom_1_data[7:0]};  // Bit_Extender bit_extender_3
  _32_bit_RF u_32_bit_rf_1 (
    .Data_In(ram_1_data), .Data_Out_1(n32_bit_rf_1_data_out_1), .Read_Address_1(bit_extender_1_out),
    .Write_Address(bit_extender_2_out), .Reg_Write(in_5), .in_6(CLK));  // open: Data_Out_2, Read_Address_2
  Bit_Extender #(.out_width(2)) bit_extender_4 (.in(rom_1_data[31:24]), .out(bit_extender_4_out));
  _32_bit_ALU u_32_bit_alu_1 (
    .CarryIn(Cin), .A(n32_bit_rf_1_data_out_1), .ALU_Operation(bit_extender_4_out), .B(bit_extender_3_out),
    .Result(n32_bit_alu_1_result), .out_9(Cout));  // open: in_2, Overflow, Zero
  RAM #(.dataWidth(32), .bus("separate")) ram_1 (
    .addr(in_1), .din(n32_bit_alu_1_result), .data(ram_1_data), .str(in_3), .clk(CLK), .ld(in_4));  // open: sel, clr

  // Notes on the sheet:
  //   (add)->02
  //   Instruction: addi $t3, $s1, 50 (Add Immediate)
  //   Seqence: OPcode  |         rs/rt         |          rd          |     immediate
  //   $s1($17)->11
  //   $t3($11)->0b
  //   IF
  //   contents of rom_1 (hex, n*v repeats v):
  //   2110050 b00
  //   50
  //   ID
  //   Fig: 32-bit Processor
  //   EX
  //   MEM
  //   WB
endmodule

module _1_bit_ALU (
  input  A,
  input  B,
  input  CarryIn,
  input  [1:0] S1S0,
  output Result,
  output Cout
);

  wire adder_1_out, and_1_out, and_2_out, multiplexer_1_out, not_1_out, or_1_out;

  Multiplexer #(.enable("false")) multiplexer_1 (.in0(B), .in1(not_1_out), .out(multiplexer_1_out), .sel(and_1_out));
  not not_1 (not_1_out, B);
  and and_1 (and_1_out, S1S0[0], S1S0[1]);
  and and_2 (and_2_out, A, B);
  or or_1 (or_1_out, A, B);
  Adder #(.width(1)) adder_1 (.a(A), .b(multiplexer_1_out), .out(adder_1_out), .cin(CarryIn), .cout(Cout));
  Multiplexer #(.select(2), .enable("false")) multiplexer_2 (
    .in0(and_2_out), .in1(or_1_out), .in2(adder_1_out), .in3(adder_1_out), .out(Result), .sel(S1S0));
endmodule

module _32_bit_ALU (
  input  CarryIn,
  input  in_2,
  input  [31:0] A,
  input  [1:0] ALU_Operation,
  input  [31:0] B,
  output [31:0] Result,
  output Overflow,
  output Zero,
  output out_9
);

  wire and_1_out, multiplexer_1_out, n1_bit_alu_1_cout, n1_bit_alu_2_cout, n1_bit_alu_3_cout,
       n1_bit_alu_4_cout, n1_bit_alu_5_cout, n1_bit_alu_6_cout, n1_bit_alu_7_cout, n1_bit_alu_8_cout,
       n1_bit_alu_9_cout, n1_bit_alu_10_cout, n1_bit_alu_11_cout, n1_bit_alu_12_cout, n1_bit_alu_13_cout,
       n1_bit_alu_14_cout, n1_bit_alu_15_cout, n1_bit_alu_16_cout, n1_bit_alu_17_cout, n1_bit_alu_18_cout,
       n1_bit_alu_19_cout, n1_bit_alu_20_cout, n1_bit_alu_21_cout, n1_bit_alu_22_cout, n1_bit_alu_23_cout,
       n1_bit_alu_24_cout, n1_bit_alu_25_cout, n1_bit_alu_26_cout, n1_bit_alu_27_cout, n1_bit_alu_28_cout,
       n1_bit_alu_29_cout, n1_bit_alu_30_cout, n1_bit_alu_31_cout;

  Multiplexer #(.enable("false")) multiplexer_1 (.in0(CarryIn), .in1(in_2), .out(multiplexer_1_out), .sel(and_1_out));
  and and_1 (and_1_out, ALU_Operation[0], ALU_Operation[1]);
  _1_bit_ALU u_1_bit_alu_1 (
    .A(A[0]), .B(B[0]), .CarryIn(multiplexer_1_out), .S1S0(ALU_Operation), .Result(Result[0]),
    .Cout(n1_bit_alu_1_cout));
  _1_bit_ALU u_1_bit_alu_2 (
    .A(A[1]), .B(B[1]), .CarryIn(n1_bit_alu_1_cout), .S1S0(ALU_Operation), .Result(Result[1]),
    .Cout(n1_bit_alu_2_cout));
  _1_bit_ALU u_1_bit_alu_3 (
    .A(A[2]), .B(B[2]), .CarryIn(n1_bit_alu_2_cout), .S1S0(ALU_Operation), .Result(Result[2]),
    .Cout(n1_bit_alu_3_cout));
  _1_bit_ALU u_1_bit_alu_4 (
    .A(A[3]), .B(B[3]), .CarryIn(n1_bit_alu_3_cout), .S1S0(ALU_Operation), .Result(Result[3]),
    .Cout(n1_bit_alu_4_cout));
  _1_bit_ALU u_1_bit_alu_5 (
    .A(A[4]), .B(B[4]), .CarryIn(n1_bit_alu_4_cout), .S1S0(ALU_Operation), .Result(Result[4]),
    .Cout(n1_bit_alu_5_cout));
  _1_bit_ALU u_1_bit_alu_6 (
    .A(A[5]), .B(B[5]), .CarryIn(n1_bit_alu_5_cout), .S1S0(ALU_Operation), .Result(Result[5]),
    .Cout(n1_bit_alu_6_cout));
  _1_bit_ALU u_1_bit_alu_7 (
    .A(A[6]), .B(B[6]), .CarryIn(n1_bit_alu_6_cout), .S1S0(ALU_Operation), .Result(Result[6]),
    .Cout(n1_bit_alu_7_cout));
  _1_bit_ALU u_1_bit_alu_8 (
    .A(A[7]), .B(B[7]), .CarryIn(n1_bit_alu_7_cout), .S1S0(ALU_Operation), .Result(Result[7]),
    .Cout(n1_bit_alu_8_cout));
  _1_bit_ALU u_1_bit_alu_9 (
    .A(A[8]), .B(B[8]), .CarryIn(n1_bit_alu_8_cout), .S1S0(ALU_Operation), .Result(Result[8]),
    .Cout(n1_bit_alu_9_cout));
  _1_bit_ALU u_1_bit_alu_10 (
    .A(A[9]), .B(B[9]), .CarryIn(n1_bit_alu_9_cout), .S1S0(ALU_Operation), .Result(Result[9]),
    .Cout(n1_bit_alu_10_cout));
  _1_bit_ALU u_1_bit_alu_11 (
    .A(A[10]), .B(B[10]), .CarryIn(n1_bit_alu_10_cout), .S1S0(ALU_Operation), .Result(Result[10]),
    .Cout(n1_bit_alu_11_cout));
  _1_bit_ALU u_1_bit_alu_12 (
    .A(A[11]), .B(B[11]), .CarryIn(n1_bit_alu_11_cout), .S1S0(ALU_Operation), .Result(Result[11]),
    .Cout(n1_bit_alu_12_cout));
  _1_bit_ALU u_1_bit_alu_13 (
    .A(A[12]), .B(B[12]), .CarryIn(n1_bit_alu_12_cout), .S1S0(ALU_Operation), .Result(Result[12]),
    .Cout(n1_bit_alu_13_cout));
  _1_bit_ALU u_1_bit_alu_14 (
    .A(A[13]), .B(B[13]), .CarryIn(n1_bit_alu_13_cout), .S1S0(ALU_Operation), .Result(Result[13]),
    .Cout(n1_bit_alu_14_cout));
  _1_bit_ALU u_1_bit_alu_15 (
    .A(A[14]), .B(B[14]), .CarryIn(n1_bit_alu_14_cout), .S1S0(ALU_Operation), .Result(Result[14]),
    .Cout(n1_bit_alu_15_cout));
  _1_bit_ALU u_1_bit_alu_16 (
    .A(A[15]), .B(B[15]), .CarryIn(n1_bit_alu_15_cout), .S1S0(ALU_Operation), .Result(Result[15]),
    .Cout(n1_bit_alu_16_cout));
  _1_bit_ALU u_1_bit_alu_17 (
    .A(A[16]), .B(B[16]), .CarryIn(n1_bit_alu_16_cout), .S1S0(ALU_Operation), .Result(Result[16]),
    .Cout(n1_bit_alu_17_cout));
  _1_bit_ALU u_1_bit_alu_18 (
    .A(A[17]), .B(B[17]), .CarryIn(n1_bit_alu_17_cout), .S1S0(ALU_Operation), .Result(Result[17]),
    .Cout(n1_bit_alu_18_cout));
  _1_bit_ALU u_1_bit_alu_19 (
    .A(A[18]), .B(B[18]), .CarryIn(n1_bit_alu_18_cout), .S1S0(ALU_Operation), .Result(Result[18]),
    .Cout(n1_bit_alu_19_cout));
  _1_bit_ALU u_1_bit_alu_20 (
    .A(A[19]), .B(B[19]), .CarryIn(n1_bit_alu_19_cout), .S1S0(ALU_Operation), .Result(Result[19]),
    .Cout(n1_bit_alu_20_cout));
  _1_bit_ALU u_1_bit_alu_21 (
    .A(A[20]), .B(B[20]), .CarryIn(n1_bit_alu_20_cout), .S1S0(ALU_Operation), .Result(Result[20]),
    .Cout(n1_bit_alu_21_cout));
  _1_bit_ALU u_1_bit_alu_22 (
    .A(A[21]), .B(B[21]), .CarryIn(n1_bit_alu_21_cout), .S1S0(ALU_Operation), .Result(Result[21]),
    .Cout(n1_bit_alu_22_cout));
  _1_bit_ALU u_1_bit_alu_23 (
    .A(A[22]), .B(B[22]), .CarryIn(n1_bit_alu_22_cout), .S1S0(ALU_Operation), .Result(Result[22]),
    .Cout(n1_bit_alu_23_cout));
  _1_bit_ALU u_1_bit_alu_24 (
    .A(A[23]), .B(B[23]), .CarryIn(n1_bit_alu_23_cout), .S1S0(ALU_Operation), .Result(Result[23]),
    .Cout(n1_bit_alu_24_cout));
  _1_bit_ALU u_1_bit_alu_25 (
    .A(A[24]), .B(B[24]), .CarryIn(n1_bit_alu_24_cout), .S1S0(ALU_Operation), .Result(Result[24]),
    .Cout(n1_bit_alu_25_cout));
  _1_bit_ALU u_1_bit_alu_26 (
    .A(A[25]), .B(B[25]), .CarryIn(n1_bit_alu_25_cout), .S1S0(ALU_Operation), .Result(Result[25]),
    .Cout(n1_bit_alu_26_cout));
  _1_bit_ALU u_1_bit_alu_27 (
    .A(A[26]), .B(B[26]), .CarryIn(n1_bit_alu_26_cout), .S1S0(ALU_Operation), .Result(Result[26]),
    .Cout(n1_bit_alu_27_cout));
  _1_bit_ALU u_1_bit_alu_28 (
    .A(A[27]), .B(B[27]), .CarryIn(n1_bit_alu_27_cout), .S1S0(ALU_Operation), .Result(Result[27]),
    .Cout(n1_bit_alu_28_cout));
  _1_bit_ALU u_1_bit_alu_29 (
    .A(A[28]), .B(B[28]), .CarryIn(n1_bit_alu_28_cout), .S1S0(ALU_Operation), .Result(Result[28]),
    .Cout(n1_bit_alu_29_cout));
  _1_bit_ALU u_1_bit_alu_30 (
    .A(A[29]), .B(B[29]), .CarryIn(n1_bit_alu_29_cout), .S1S0(ALU_Operation), .Result(Result[29]),
    .Cout(n1_bit_alu_30_cout));
  _1_bit_ALU u_1_bit_alu_31 (
    .A(A[30]), .B(B[30]), .CarryIn(n1_bit_alu_30_cout), .S1S0(ALU_Operation), .Result(Result[30]),
    .Cout(n1_bit_alu_31_cout));
  _1_bit_ALU u_1_bit_alu_32 (
    .A(A[31]), .B(B[31]), .CarryIn(n1_bit_alu_31_cout), .S1S0(ALU_Operation), .Result(Result[31]),
    .Cout(out_9));
  and and_2 (Overflow, A[31], B[31]);
  nor nor_1 (Zero, Result[0], Result[1], Result[2], Result[3], Result[4], Result[5], Result[6], Result[7], Result[8], Result[9], Result[10], Result[11], Result[12], Result[13], Result[14], Result[15], Result[16], Result[17], Result[18], Result[19], Result[20], Result[21], Result[22], Result[23], Result[24], Result[25], Result[26], Result[27], Result[28], Result[29], Result[30], Result[31]);

  // Other names for the same wires on the sheet: ALU_OP[1:0] = ALU_Operation; R0 = Result[0]; R1 = Result[1];
  //   R2 = Result[2]; R3 = Result[3]; R4 = Result[4]; R5 = Result[5]; R6 = Result[6]; R7 = Result[7]; R8 = Result[8];
  //   R9 = Result[9]; R10 = Result[10]; R11 = Result[11]; R12 = Result[12]; R13 = Result[13]; R14 = Result[14];
  //   R15 = Result[15]; R16 = Result[16]; R17 = Result[17]; R18 = Result[18]; R19 = Result[19]; R20 = Result[20];
  //   R21 = Result[21]; R22 = Result[22]; R23 = Result[23]; R24 = Result[24]; R25 = Result[25]; R26 = Result[26];
  //   R27 = Result[27]; R28 = Result[28]; R29 = Result[29]; R30 = Result[30]; R31 = Result[31]
endmodule

module _32_bit_RF (
  input  [31:0] Data_In,
  input  Reg_Write,
  input  [4:0] Read_Address_1,
  input  [4:0] Write_Address,
  input  [4:0] Read_Address_2,
  input  in_6,
  output [31:0] Data_Out_1,
  output [31:0] Data_Out_2
);

  wire and_1_out, and_2_out, and_3_out, and_4_out, and_5_out, and_6_out, and_7_out, and_8_out, and_9_out,
       and_10_out, and_11_out, and_12_out, and_13_out, and_14_out, and_15_out, and_16_out, and_17_out,
       and_18_out, and_19_out, and_20_out, and_21_out, and_22_out, and_23_out, and_24_out, and_25_out,
       and_26_out, and_27_out, and_28_out, and_29_out, and_30_out, and_31_out, and_32_out, decoder_1_out0,
       decoder_1_out1, decoder_1_out2, decoder_1_out3, decoder_1_out4, decoder_1_out5, decoder_1_out6,
       decoder_1_out7, decoder_1_out8, decoder_1_out9, decoder_1_out10, decoder_1_out11, decoder_1_out12,
       decoder_1_out13, decoder_1_out14, decoder_1_out15, decoder_1_out16, decoder_1_out17, decoder_1_out18,
       decoder_1_out19, decoder_1_out20, decoder_1_out21, decoder_1_out22, decoder_1_out23, decoder_1_out24,
       decoder_1_out25, decoder_1_out26, decoder_1_out27, decoder_1_out28, decoder_1_out29, decoder_1_out30,
       decoder_1_out31;
  wire [31:0] a0_q, a1_q, a2_q, a3_q, at_q, fp_q, gp_q, k0_q, k1_q, ra_q, s0_q, s1_q, s2_q, s3_q, s4_q, s5_q,
       s6_q, s7_q, sp_q, t0_q, t1_q, t2_q, t3_q, t4_q, t5_q, t6_q, t7_q, t8_q, t9_q, v0_q, v1_q, Zero_q;

  Decoder #(.select(5), .enable("false")) decoder_1 (
    .out0(decoder_1_out0), .out1(decoder_1_out1), .out2(decoder_1_out2), .out3(decoder_1_out3),
    .out4(decoder_1_out4), .out5(decoder_1_out5), .out6(decoder_1_out6), .out7(decoder_1_out7),
    .out8(decoder_1_out8), .out9(decoder_1_out9), .out10(decoder_1_out10), .out11(decoder_1_out11),
    .out12(decoder_1_out12), .out13(decoder_1_out13), .out14(decoder_1_out14), .out15(decoder_1_out15),
    .out16(decoder_1_out16), .out17(decoder_1_out17), .out18(decoder_1_out18), .out19(decoder_1_out19),
    .out20(decoder_1_out20), .out21(decoder_1_out21), .out22(decoder_1_out22), .out23(decoder_1_out23),
    .out24(decoder_1_out24), .out25(decoder_1_out25), .out26(decoder_1_out26), .out27(decoder_1_out27),
    .out28(decoder_1_out28), .out29(decoder_1_out29), .out30(decoder_1_out30), .out31(decoder_1_out31),
    .sel(Write_Address));
  and and_1 (and_1_out, decoder_1_out0, Reg_Write);
  and and_2 (and_2_out, decoder_1_out1, Reg_Write);
  and and_3 (and_3_out, decoder_1_out2, Reg_Write);
  and and_4 (and_4_out, decoder_1_out3, Reg_Write);
  and and_5 (and_5_out, decoder_1_out4, Reg_Write);
  and and_6 (and_6_out, decoder_1_out5, Reg_Write);
  and and_7 (and_7_out, decoder_1_out6, Reg_Write);
  and and_8 (and_8_out, decoder_1_out7, Reg_Write);
  and and_9 (and_9_out, decoder_1_out8, Reg_Write);
  and and_10 (and_10_out, decoder_1_out9, Reg_Write);
  and and_11 (and_11_out, decoder_1_out10, Reg_Write);
  and and_12 (and_12_out, decoder_1_out11, Reg_Write);
  and and_13 (and_13_out, decoder_1_out12, Reg_Write);
  and and_14 (and_14_out, decoder_1_out13, Reg_Write);
  and and_15 (and_15_out, decoder_1_out14, Reg_Write);
  and and_16 (and_16_out, decoder_1_out15, Reg_Write);
  and and_17 (and_17_out, decoder_1_out16, Reg_Write);
  and and_18 (and_18_out, decoder_1_out17, Reg_Write);
  and and_19 (and_19_out, decoder_1_out18, Reg_Write);
  and and_20 (and_20_out, decoder_1_out19, Reg_Write);
  and and_21 (and_21_out, decoder_1_out20, Reg_Write);
  and and_22 (and_22_out, decoder_1_out21, Reg_Write);
  and and_23 (and_23_out, decoder_1_out22, Reg_Write);
  and and_24 (and_24_out, decoder_1_out23, Reg_Write);
  and and_25 (and_25_out, decoder_1_out24, Reg_Write);
  and and_26 (and_26_out, decoder_1_out25, Reg_Write);
  and and_27 (and_27_out, decoder_1_out26, Reg_Write);
  and and_28 (and_28_out, decoder_1_out27, Reg_Write);
  and and_29 (and_29_out, decoder_1_out28, Reg_Write);
  and and_30 (and_30_out, decoder_1_out29, Reg_Write);
  and and_31 (and_31_out, decoder_1_out30, Reg_Write);
  and and_32 (and_32_out, decoder_1_out31, Reg_Write);
  Register #(.width(32)) Zero (.D(Data_In), .en(and_1_out), .Q(Zero_q), .clk(in_6));  // open: clr
  Register #(.width(32)) at (.D(Data_In), .en(and_2_out), .Q(at_q), .clk(in_6));  // open: clr
  Register #(.width(32)) v0 (.D(Data_In), .en(and_3_out), .Q(v0_q), .clk(in_6));  // open: clr
  Register #(.width(32)) v1 (.D(Data_In), .en(and_4_out), .Q(v1_q), .clk(in_6));  // open: clr
  Register #(.width(32)) a0 (.D(Data_In), .en(and_5_out), .Q(a0_q), .clk(in_6));  // open: clr
  Register #(.width(32)) a1 (.D(Data_In), .en(and_6_out), .Q(a1_q), .clk(in_6));  // open: clr
  Register #(.width(32)) a2 (.D(Data_In), .en(and_7_out), .Q(a2_q), .clk(in_6));  // open: clr
  Register #(.width(32)) a3 (.D(Data_In), .en(and_8_out), .Q(a3_q), .clk(in_6));  // open: clr
  Register #(.width(32)) t0 (.D(Data_In), .en(and_9_out), .Q(t0_q), .clk(in_6));  // open: clr
  Register #(.width(32)) t1 (.D(Data_In), .en(and_10_out), .Q(t1_q), .clk(in_6));  // open: clr
  Register #(.width(32)) t2 (.D(Data_In), .en(and_11_out), .Q(t2_q), .clk(in_6));  // open: clr
  Register #(.width(32)) t3 (.D(Data_In), .en(and_12_out), .Q(t3_q), .clk(in_6));  // open: clr
  Register #(.width(32)) t4 (.D(Data_In), .en(and_13_out), .Q(t4_q), .clk(in_6));  // open: clr
  Register #(.width(32)) t5 (.D(Data_In), .en(and_14_out), .Q(t5_q), .clk(in_6));  // open: clr
  Register #(.width(32)) t6 (.D(Data_In), .en(and_15_out), .Q(t6_q), .clk(in_6));  // open: clr
  Register #(.width(32)) t7 (.D(Data_In), .en(and_16_out), .Q(t7_q), .clk(in_6));  // open: clr
  Register #(.width(32)) s0 (.D(Data_In), .en(and_17_out), .Q(s0_q), .clk(in_6));  // open: clr
  Register #(.width(32)) s1 (.D(Data_In), .en(and_18_out), .Q(s1_q), .clk(in_6));  // open: clr
  Register #(.width(32)) s2 (.D(Data_In), .en(and_19_out), .Q(s2_q), .clk(in_6));  // open: clr
  Register #(.width(32)) s3 (.D(Data_In), .en(and_20_out), .Q(s3_q), .clk(in_6));  // open: clr
  Register #(.width(32)) s4 (.D(Data_In), .en(and_21_out), .Q(s4_q), .clk(in_6));  // open: clr
  Register #(.width(32)) s5 (.D(Data_In), .en(and_22_out), .Q(s5_q), .clk(in_6));  // open: clr
  Register #(.width(32)) s6 (.D(Data_In), .en(and_23_out), .Q(s6_q), .clk(in_6));  // open: clr
  Register #(.width(32)) s7 (.D(Data_In), .en(and_24_out), .Q(s7_q), .clk(in_6));  // open: clr
  Register #(.width(32)) t8 (.D(Data_In), .en(and_25_out), .Q(t8_q), .clk(in_6));  // open: clr
  Register #(.width(32)) t9 (.D(Data_In), .en(and_26_out), .Q(t9_q), .clk(in_6));  // open: clr
  Register #(.width(32)) k0 (.D(Data_In), .en(and_27_out), .Q(k0_q), .clk(in_6));  // open: clr
  Register #(.width(32)) k1 (.D(Data_In), .en(and_28_out), .Q(k1_q), .clk(in_6));  // open: clr
  Register #(.width(32)) gp (.D(Data_In), .en(and_29_out), .Q(gp_q), .clk(in_6));  // open: clr
  Register #(.width(32)) sp (.D(Data_In), .en(and_30_out), .Q(sp_q), .clk(in_6));  // open: clr
  Register #(.width(32)) fp (.D(Data_In), .en(and_31_out), .Q(fp_q), .clk(in_6));  // open: clr
  Register #(.width(32)) ra (.D(Data_In), .en(and_32_out), .Q(ra_q), .clk(in_6));  // open: clr
  Multiplexer #(.select(5), .width(32), .enable("false")) multiplexer_1 (
    .in0(Zero_q), .in1(at_q), .in2(v0_q), .in3(v1_q), .in4(a0_q), .in5(a1_q), .in6(a2_q), .in7(a3_q),
    .in8(t0_q), .in9(t1_q), .in10(t2_q), .in11(t3_q), .in12(t4_q), .in13(t5_q), .in14(t6_q), .in15(t7_q),
    .in16(s0_q), .in17(s1_q), .in18(s2_q), .in19(s3_q), .in20(s4_q), .in21(s5_q), .in22(s6_q), .in23(s7_q),
    .in24(t8_q), .in25(t9_q), .in26(k0_q), .in27(k1_q), .in28(gp_q), .in29(sp_q), .in30(fp_q), .in31(ra_q),
    .out(Data_Out_1), .sel(Read_Address_1));
  Multiplexer #(.select(5), .width(32), .enable("false")) multiplexer_2 (
    .in0(Zero_q), .in1(at_q), .in2(v0_q), .in3(v1_q), .in4(a0_q), .in5(a1_q), .in6(a2_q), .in7(a3_q),
    .in8(t0_q), .in9(t1_q), .in10(t2_q), .in11(t3_q), .in12(t4_q), .in13(t5_q), .in14(t6_q), .in15(t7_q),
    .in16(s0_q), .in17(s1_q), .in18(s2_q), .in19(s3_q), .in20(s4_q), .in21(s5_q), .in22(s6_q), .in23(s7_q),
    .in24(t8_q), .in25(t9_q), .in26(k0_q), .in27(k1_q), .in28(gp_q), .in29(sp_q), .in30(fp_q), .in31(ra_q),
    .out(Data_Out_2), .sel(Read_Address_2));
endmodule

module R_Type_Datapath (
  input  Cin,
  input  in_2,
  input  CLK,
  output Cout
);

  wire [1:0] bit_extender_4_out;
  wire [4:0] bit_extender_1_out, bit_extender_2_out;
  wire [7:0] adder_1_out, PC_q;
  wire [31:0] bit_extender_3_out, n32_bit_alu_1_result, n32_bit_rf_1_data_out_1, rom_1_data;

  Register PC (.D(adder_1_out), .Q(PC_q), .clk(CLK));  // open: en, clr
  Adder adder_1 (.a(PC_q), .b(8'h1), .out(adder_1_out));  // open: cin, cout
  ROM #(.dataWidth(32)) rom_1 (.addr(PC_q), .data(rom_1_data));  // open: sel
  Bit_Extender #(.out_width(5)) bit_extender_1 (.in(rom_1_data[23:16]), .out(bit_extender_1_out));
  Bit_Extender #(.out_width(5)) bit_extender_2 (.in(rom_1_data[15:8]), .out(bit_extender_2_out));
  assign bit_extender_3_out = {{24{1'b0}}, rom_1_data[7:0]};  // Bit_Extender bit_extender_3
  _32_bit_RF u_32_bit_rf_1 (
    .Data_In(n32_bit_alu_1_result), .Data_Out_1(n32_bit_rf_1_data_out_1),
    .Read_Address_1(bit_extender_1_out), .Write_Address(bit_extender_2_out), .Reg_Write(in_2), .in_6(CLK));  // open: Data_Out_2, Read_Address_2
  Bit_Extender #(.out_width(2)) bit_extender_4 (.in(rom_1_data[31:24]), .out(bit_extender_4_out));
  _32_bit_ALU u_32_bit_alu_1 (
    .CarryIn(Cin), .A(n32_bit_rf_1_data_out_1), .ALU_Operation(bit_extender_4_out), .B(bit_extender_3_out),
    .Result(n32_bit_alu_1_result), .out_9(Cout));  // open: in_2, Overflow, Zero

  // Notes on the sheet:
  //   IF
  //   ID
  //   EX
endmodule
