// Logisim project Lab_6_16 bit alu.circ as structural Verilog: 2 circuits, main circuit main
module main (
  input  A,
  input  B,
  input  CarryIn,
  input  [1:0] S1S0,
  output Result,
  output Cout
);

  wire adder_1_out, and_1_out, and_2_out, multiplexer_1_out, not_1_out, or_1_out;

  Multiplexer #(.enable("false")) multiplexer_1 (.in0(B), .in1(not_1_out), .out(multiplexer_1_out), .sel(and_1_out));
  not not_1 (not_1_out, B);
  and and_1 (and_1_out, S1S0[0], S1S0[1]);
  and and_2 (and_2_out, A, B);
  or or_1 (or_1_out, A, B);
  Adder #(.width(1)) adder_1 (.a(A), .b(multiplexer_1_out), .out(adder_1_out), .cin(CarryIn), .cout(Cout));
  Multiplexer #(.select(2), .enable("false")) multiplexer_2 (
    .in0(and_2_out), .in1(or_1_out), .in2(adder_1_out), .in3(adder_1_out), .out(Result), .sel(S1S0));
endmodule

module _16bit_Alu (
  input  CarryIn,
  input  [15:0] A,
  input  [15:0] B,
  input  [1:0] S1S0,
  output [15:0] Result,
  output Cout
);

  wire main_1_cout, main_2_cout, main_3_cout, main_4_cout, main_5_cout, main_6_cout, main_7_cout,
       main_8_cout, main_9_cout, main_10_cout, main_11_cout, main_12_cout, main_13_cout, main_14_cout,
       main_15_cout;

  main main_1 (.A(A[0]), .B(B[0]), .CarryIn(CarryIn), .S1S0(S1S0), .Result(Result[0]), .Cout(main_1_cout));
  main main_2 (.A(A[1]), .B(B[1]), .CarryIn(main_1_cout), .S1S0(S1S0), .Result(Result[1]), .Cout(main_2_cout));
  main main_3 (.A(A[2]), .B(B[2]), .CarryIn(main_2_cout), .S1S0(S1S0), .Result(Result[2]), .Cout(main_3_cout));
  main main_4 (.A(A[3]), .B(B[3]), .CarryIn(main_3_cout), .S1S0(S1S0), .Result(Result[3]), .Cout(main_4_cout));
  main main_5 (.A(A[4]), .B(B[4]), .CarryIn(main_4_cout), .S1S0(S1S0), .Result(Result[4]), .Cout(main_5_cout));
  main main_6 (.A(A[5]), .B(B[5]), .CarryIn(main_5_cout), .S1S0(S1S0), .Result(Result[5]), .Cout(main_6_cout));
  main main_7 (.A(A[6]), .B(B[6]), .CarryIn(main_6_cout), .S1S0(S1S0), .Result(Result[6]), .Cout(main_7_cout));
  main main_8 (.A(A[7]), .B(B[7]), .CarryIn(main_7_cout), .S1S0(S1S0), .Result(Result[7]), .Cout(main_8_cout));
  main main_9 (.A(A[8]), .B(B[8]), .CarryIn(main_8_cout), .S1S0(S1S0), .Result(Result[8]), .Cout(main_9_cout));
  main main_10 (.A(A[9]), .B(B[9]), .CarryIn(main_9_cout), .S1S0(S1S0), .Result(Result[9]), .Cout(main_10_cout));
  main main_11 (.A(A[10]), .B(B[10]), .CarryIn(main_10_cout), .S1S0(S1S0), .Result(Result[10]), .Cout(main_11_cout));
  main main_12 (.A(A[11]), .B(B[11]), .CarryIn(main_11_cout), .S1S0(S1S0), .Result(Result[11]), .Cout(main_12_cout));
  main main_13 (.A(A[12]), .B(B[12]), .CarryIn(main_12_cout), .S1S0(S1S0), .Result(Result[12]), .Cout(main_13_cout));
  main main_14 (.A(A[13]), .B(B[13]), .CarryIn(main_13_cout), .S1S0(S1S0), .Result(Result[13]), .Cout(main_14_cout));
  main main_15 (.A(A[14]), .B(B[14]), .CarryIn(main_14_cout), .S1S0(S1S0), .Result(Result[14]), .Cout(main_15_cout));
  main main_16 (.A(A[15]), .B(B[15]), .CarryIn(main_15_cout), .S1S0(S1S0), .Result(Result[15]), .Cout(Cout));
endmodule
